// Logisim project SR_flip_flop.circ as structural Verilog: 1 circuit, main circuit main
module main (
  input  in_1,
  input  in_2,
  input  s,
  input  r,
  input  clk,
  output out_6,
  output out_7,
  output out_8,
  output out_9,
  output out_10,
  output Q,
  output Q_prime,
  output Q_2,
  output Q_prime_2,
  output Q_3,
  output Q_prime_3
);

  wire clock_1_out, n7400_2_pin1, n7400_2_pin5, nand_2_out, nand_3_out;

  _7400 u_7400_1 (
    .pin1(in_2), .pin2(in_1), .pin3(out_9), .pin4(in_1), .pin5(in_2), .pin6(out_10), .pin13(in_1),
    .pin12(in_2), .pin11(out_7), .pin10(in_1), .pin9(in_2), .pin8(out_8));
  _7400 u_7400_2 (
    .pin1(n7400_2_pin1), .pin2(Q_prime_3), .pin3(Q_3), .pin4(Q_3), .pin5(n7400_2_pin5), .pin6(Q_prime_3),
    .pin13(s), .pin12(clk), .pin11(n7400_2_pin1), .pin10(r), .pin9(clk), .pin8(n7400_2_pin5));
  nand nand_1 (out_6, in_1, in_2);
  nand nand_2 (nand_2_out, s, clk);
  nand nand_3 (nand_3_out, r, clk);
  nand nand_4 (Q, nand_2_out, Q_prime);
  nand nand_5 (Q_prime, Q, nand_3_out);
  Clock clock_1 (.out(clock_1_out));
  S_R_Flip_Flop s_r_ff_1 (.S(s), .R(r), .clk(clock_1_out), .Q(Q_2), .Qn(Q_prime_2));  // open: reset, preset

  // Notes on the sheet:
  //   Simple NAND
  //   SR Flip-flop
  //   (simulation will crush if both s and r is set to 1)
  //   clk
endmodule
