// Logisim project counters.circ as structural Verilog: 1 circuit, main circuit main
module main (
  output out_1,
  output out_2,
  output out_3,
  output out_4
);

  wire clock_1_out, not_1_out, not_2_out, not_3_out;

  T_Flip_Flop t_ff_1 (.T(1'b1), .clk(not_1_out), .Q(out_1));  // open: Qn, reset, preset
  T_Flip_Flop t_ff_2 (.T(1'b1), .clk(not_2_out), .Q(out_2));  // open: Qn, reset, preset
  not not_1 (not_1_out, out_2);
  T_Flip_Flop t_ff_3 (.T(1'b1), .clk(not_3_out), .Q(out_3));  // open: Qn, reset, preset
  not not_2 (not_2_out, out_3);
  Clock clock_1 (.out(clock_1_out));
  T_Flip_Flop t_ff_4 (.T(1'b1), .clk(clock_1_out), .Q(out_4));  // open: Qn, reset, preset
  not not_3 (not_3_out, out_4);

  // Notes on the sheet:
  //   Asynchronus counter (ripple)
endmodule
