// Logisim project universal_shift_register.circ as structural Verilog: 1 circuit, main circuit main
module main (
  input  in_1,
  input  in_2,
  input  in_3,
  input  in_4,
  input  in_5,
  input  left_shift_input,
  input  [1:0] in_7,
  output out_8,
  output out_9,
  output out_10,
  output out_11
);

  wire multiplexer_1_out, multiplexer_2_out, multiplexer_3_out, multiplexer_4_out;

  Multiplexer #(.select(2)) multiplexer_1 (
    .in0(out_8), .in1(in_1), .in2(out_9), .in3(in_2), .out(multiplexer_1_out), .sel(in_7));
  Multiplexer #(.select(2)) multiplexer_2 (
    .in0(out_9), .in1(out_8), .in2(out_10), .in3(in_3), .out(multiplexer_2_out), .sel(in_7));
  Multiplexer #(.select(2)) multiplexer_3 (
    .in0(out_10), .in1(out_9), .in2(out_11), .in3(in_4), .out(multiplexer_3_out), .sel(in_7));
  Multiplexer #(.select(2)) multiplexer_4 (
    .in0(out_11), .in1(out_10), .in2(left_shift_input), .in3(in_5), .out(multiplexer_4_out), .sel(in_7));
  D_Flip_Flop d_ff_1 (.D(multiplexer_1_out), .Q(out_8));  // open: clk, Qn, preset, reset
  D_Flip_Flop d_ff_2 (.D(multiplexer_2_out), .Q(out_9));  // open: clk, Qn, preset, reset
  D_Flip_Flop d_ff_3 (.D(multiplexer_3_out), .Q(out_10));  // open: clk, Qn, preset, reset
  D_Flip_Flop d_ff_4 (.D(multiplexer_4_out), .Q(out_11));  // open: clk, Qn, preset, reset

  // Notes on the sheet:
  //   selection
  //   right-shift input
endmodule
